// Logisim project basicgates.circ as structural Verilog: 3 circuits, main circuit main
module main (
);

  wire adder2bit_1_overflow;
  wire [1:0] adder2bit_1_output1;

  // Probe on adder2bit_1_overflow
  adder2bit adder2bit_1 (
    .inflow(1'b1), .input1(2'b11), .input2(2'b11), .overflow(adder2bit_1_overflow),
    .output1(adder2bit_1_output1));
  // Probe on adder2bit_1_output1
endmodule

module adder1bit (
  input  inflow,
  input  input1,
  input  input2,
  output overflow,
  output output1
);

  wire and_1_out, and_2_out, xor_1_out;

  and and_1 (and_1_out, input1, input2);
  xor xor_1 (xor_1_out, input1, input2);
  and and_2 (and_2_out, inflow, xor_1_out);
  xor xor_2 (output1, inflow, xor_1_out);
  or or_1 (overflow, and_1_out, and_2_out);
endmodule

module adder2bit (
  input  inflow,
  input  [1:0] input1,
  input  [1:0] input2,
  output overflow,
  output [1:0] output1
);

  wire adder1bit_1_overflow;

  adder1bit adder1bit_1 (
    .inflow(inflow), .input1(input1[0]), .input2(input2[0]), .overflow(adder1bit_1_overflow),
    .output1(output1[0]));
  adder1bit adder1bit_2 (
    .inflow(adder1bit_1_overflow), .input1(input1[1]), .input2(input2[1]), .overflow(overflow),
    .output1(output1[1]));
endmodule
