// Logisim project muxrisccore.circ as structural Verilog: 2 circuits, main circuit main
module main (
);

  wire and_1_out, and_2_out, and_3_out, and_4_out, and_5_out, bitselector_11_out, bitselector_12_out,
       clock_1_out, clock_2_out, clock_3_out, clock_4_out, clock_5_out, comparator_1_eq, comparator_3_eq,
       comparator_4_eq, comparator_5_eq, comparator_6_eq, comparator_7_eq, comparator_7_lt, comparator_8_eq,
       comparator_8_lt, counter_1_q, fpcomparator_1_p8, fpcomparator_1_p9, multiplexer_1_out,
       multiplexer_5_out, not_1_out, not_2_out, not_3_out, or_1_out, or_2_out, or_4_out, or_5_out,
       register_3_q;
  wire [1:0] bitselector_9_out;
  wire [3:0] bitselector_8_out;
  wire [5:0] bitselector_5_out, bitselector_6_out, bitselector_7_out, bitselector_10_out;
  wire [15:0] bitselector_1_out, bitselector_2_out, bitselector_3_out, bitselector_4_out, bitselector_13_out,
       bitselector_14_out, counter_2_q, multiplexer_3_out, multiplexer_4_out;
  wire [63:0] fpcomparator_1_p6, multiplexer_2_out, multiplexer_6_out, or_3_out, ram_1_dout, register_1_q,
       register_2_q, registry_1_regxout, shifter_1_out;

  BitSelector #(.group(16), .width(64)) bitselector_1 (.in(register_1_q), .out(bitselector_1_out), .sel(2'b11));
  BitSelector #(.group(16), .width(64)) bitselector_2 (.in(register_1_q), .out(bitselector_2_out), .sel(2'b10));
  BitSelector #(.group(16), .width(64)) bitselector_3 (.in(register_1_q), .out(bitselector_3_out), .sel(2'b01));
  BitSelector #(.group(16), .width(64)) bitselector_4 (.in(register_1_q), .out(bitselector_4_out), .sel(2'b00));
  Register #(.trigger("falling"), .width(64)) register_1 (
    .D(ram_1_dout), .en(or_1_out), .clk(clock_1_out), .Q(register_1_q));  // open: clr
  or or_1 (or_1_out, or_4_out, comparator_1_eq);
  Comparator #(.width(64)) comparator_1 (.a({64{1'b0}}), .b(register_1_q), .eq(comparator_1_eq));  // open: gt, lt
  Clock clock_1 (.out(clock_1_out));
  BitSelector #(.group(6), .width(16)) bitselector_5 (.in(bitselector_1_out), .out(bitselector_5_out), .sel(2'b00));
  BitSelector #(.group(6), .width(16)) bitselector_6 (.in(bitselector_2_out), .out(bitselector_6_out), .sel(2'b00));
  BitSelector #(.group(6), .width(16)) bitselector_7 (.in(bitselector_3_out), .out(bitselector_7_out), .sel(2'b00));
  BitSelector #(.group(4), .width(16)) bitselector_8 (.in(bitselector_4_out), .out(bitselector_8_out), .sel(2'b00));
  BitSelector #(.group(2), .width(16)) bitselector_9 (.in(bitselector_3_out), .out(bitselector_9_out), .sel(3'b100));
  BitSelector #(.group(6), .width(16)) bitselector_10 (.in(bitselector_3_out), .out(bitselector_10_out), .sel(2'b00));
  BitSelector #(.width(64)) bitselector_11 (.in(fpcomparator_1_p6), .out(bitselector_11_out), .sel(bitselector_7_out));
  Comparator #(.mode("unsigned"), .width(4)) comparator_2 (.a(bitselector_8_out), .b(4'b0000));  // open: gt, eq, lt
  Comparator #(.mode("unsigned"), .width(4)) comparator_3 (
    .a(bitselector_8_out), .b(4'b0001), .eq(comparator_3_eq));  // open: gt, lt
  Comparator #(.mode("unsigned"), .width(4)) comparator_4 (
    .a(bitselector_8_out), .b(4'b0010), .eq(comparator_4_eq));  // open: gt, lt
  Comparator #(.mode("unsigned"), .width(4)) comparator_5 (
    .a(bitselector_8_out), .b(4'b0011), .eq(comparator_5_eq));  // open: gt, lt
  Counter #(.max('h1), .trigger("falling"), .width(1)) counter_1 (
    .count(comparator_5_eq), .Q(counter_1_q), .clk(clock_2_out), .clr(not_1_out));  // open: load, D, carry, up
  not not_1 (not_1_out, comparator_5_eq);
  Clock clock_2 (.out(clock_2_out));
  BitSelector #(.width(16)) bitselector_12 (.in(bitselector_3_out), .out(bitselector_12_out), .sel(4'b0000));
  Comparator #(.mode("unsigned"), .width(4)) comparator_6 (
    .a(bitselector_8_out), .b(4'b0100), .eq(comparator_6_eq));  // open: gt, lt
  Multiplexer #(.select(2)) multiplexer_1 (
    .in0(comparator_7_eq), .in1(comparator_7_lt), .in2(fpcomparator_1_p8), .in3(fpcomparator_1_p9),
    .out(multiplexer_1_out), .sel(bitselector_9_out));
  Comparator #(.width(64)) comparator_7 (
    .a(fpcomparator_1_p6), .b({64{1'b0}}), .eq(comparator_7_eq), .lt(comparator_7_lt));  // open: gt
  // FPComparator #(.fpwidth(64)) fpcomparator_1: pin names not known; wires that end beside it: register_1_q, bitselector_1_out, bitselector_2_out, bitselector_3_out, bitselector_8_out, fpcomparator_1_p6, {64{1'b0}}, fpcomparator_1_p8, fpcomparator_1_p9
  and and_1 (and_1_out, bitselector_11_out, comparator_3_eq);
  or or_2 (or_2_out, comparator_4_eq, and_3_out, and_5_out);
  and and_2 (and_2_out, comparator_5_eq, comparator_8_lt);
  and and_3 (and_3_out, comparator_8_eq, not_2_out);
  not not_2 (not_2_out, bitselector_12_out);
  Comparator #(.mode("unsigned"), .width(1)) comparator_8 (
    .a(counter_1_q), .b(1'b1), .eq(comparator_8_eq), .lt(comparator_8_lt));  // open: gt
  and and_4 (and_4_out, comparator_8_eq, bitselector_12_out);
  and and_5 (and_5_out, comparator_6_eq, multiplexer_1_out);
  assign or_3_out = shifter_1_out | registry_1_regxout;  // OR_Gate or_3, 64 bits wide
  Shifter #(.width(64)) shifter_1 (.in(64'h1), .\dist (bitselector_10_out), .out(shifter_1_out));
  or or_4 (or_4_out, comparator_3_eq, or_2_out, comparator_8_eq, comparator_6_eq);
  Multiplexer #(.select(4), .width(64)) multiplexer_2 (
    .in0(ram_1_dout), .in1(ram_1_dout), .in2({{32{1'b0}}, bitselector_2_out, bitselector_3_out}),
    .in3(ram_1_dout), .in4(or_3_out), .out(multiplexer_2_out), .sel(bitselector_8_out));  // open: in5, in6, in7, in8, in9, in10, in11, in12, in13, in14, in15
  buf or_5 (or_5_out, comparator_8_eq);  // OR_Gate
  registry registry_1 (
    .value(multiplexer_2_out), .update(or_2_out), .regX(bitselector_5_out), .regY(bitselector_6_out),
    .regXout(registry_1_regxout), .regYout(fpcomparator_1_p6));
  not not_3 (not_3_out, or_5_out);
  BitSelector #(.group(16), .width(64)) bitselector_13 (.in(registry_1_regxout), .out(bitselector_13_out), .sel(2'b00));
  Register #(.width(64)) register_2 (
    .D(fpcomparator_1_p6), .en(and_2_out), .clk(clock_3_out), .Q(register_2_q));  // open: clr
  Clock clock_3 (.out(clock_3_out));
  Register #(.width(1)) register_3 (.D(and_2_out), .en(1'b1), .clk(clock_3_out), .Q(register_3_q));  // open: clr
  Counter #(.max('hffff), .width(16)) counter_2 (
    .load(and_1_out), .D(bitselector_13_out), .count(not_3_out), .Q(counter_2_q), .clk(clock_4_out));  // open: carry, up, clr
  Clock clock_4 (.out(clock_4_out));
  Multiplexer #(.width(16)) multiplexer_3 (
    .in0(counter_2_q), .in1(bitselector_14_out), .out(multiplexer_3_out), .sel(register_3_q));
  BitSelector #(.group(16), .width(64)) bitselector_14 (.in(register_2_q), .out(bitselector_14_out), .sel(2'b00));
  Multiplexer #(.select(4), .width(16)) multiplexer_4 (
    .in0(counter_2_q), .in1(counter_2_q), .in2(counter_2_q), .in3(multiplexer_3_out), .in4(counter_2_q),
    .out(multiplexer_4_out), .sel(bitselector_8_out));  // open: in5, in6, in7, in8, in9, in10, in11, in12, in13, in14, in15
  Clock clock_5 (.out(clock_5_out));
  Multiplexer #(.select(4)) multiplexer_5 (
    .in0(1'b0), .in1(1'b0), .in2(1'b0), .in3(and_4_out), .in4(1'b0), .out(multiplexer_5_out),
    .sel(bitselector_8_out));  // open: in5, in6, in7, in8, in9, in10, in11, in12, in13, in14, in15
  Multiplexer #(.select(4), .width(64)) multiplexer_6 (
    .in0({64{1'b0}}), .in1({64{1'b0}}), .in2({64{1'b0}}), .in3(registry_1_regxout), .in4({64{1'b0}}),
    .out(multiplexer_6_out), .sel(bitselector_8_out));  // open: in5, in6, in7, in8, in9, in10, in11, in12, in13, in14, in15
  RAM #(.addrWidth(16), .dataWidth(64), .enables("line"), .\type ("nonvolatile")) ram_1 (
    .addr(multiplexer_4_out), .we(multiplexer_5_out), .clk(clock_5_out), .din(multiplexer_6_out),
    .dout(ram_1_dout));
endmodule

module registry (
  input  [63:0] value,
  input  update,
  input  [5:0] regX,
  input  [5:0] regY,
  output [63:0] regXout,
  output [63:0] regYout
);

  wire clock_1_out, clock_2_out, clock_3_out, clock_4_out, clock_5_out, clock_6_out, clock_7_out,
       clock_8_out, clock_9_out, clock_10_out, clock_11_out, clock_12_out, clock_13_out, clock_14_out,
       clock_15_out, clock_16_out, clock_17_out, clock_18_out, clock_19_out, clock_20_out, clock_21_out,
       clock_22_out, clock_23_out, clock_24_out, clock_25_out, clock_26_out, clock_27_out, clock_28_out,
       clock_29_out, clock_30_out, clock_31_out, clock_32_out, clock_33_out, clock_34_out, clock_35_out,
       clock_36_out, clock_37_out, clock_38_out, clock_39_out, clock_40_out, clock_41_out, clock_42_out,
       clock_43_out, clock_44_out, clock_45_out, clock_46_out, clock_47_out, clock_48_out, clock_49_out,
       clock_50_out, clock_51_out, clock_52_out, clock_53_out, clock_54_out, clock_55_out, clock_56_out,
       clock_57_out, clock_58_out, clock_59_out, clock_60_out, clock_61_out, clock_62_out, clock_63_out,
       clock_64_out, demultiplexer_1_out0, demultiplexer_1_out1, demultiplexer_1_out2, demultiplexer_1_out3,
       demultiplexer_1_out4, demultiplexer_1_out5, demultiplexer_1_out6, demultiplexer_1_out7,
       demultiplexer_1_out8, demultiplexer_1_out9, demultiplexer_1_out10, demultiplexer_1_out11,
       demultiplexer_1_out12, demultiplexer_1_out13, demultiplexer_1_out14, demultiplexer_1_out15,
       demultiplexer_1_out16, demultiplexer_1_out17, demultiplexer_1_out18, demultiplexer_1_out19,
       demultiplexer_1_out20, demultiplexer_1_out21, demultiplexer_1_out22, demultiplexer_1_out23,
       demultiplexer_1_out24, demultiplexer_1_out25, demultiplexer_1_out26, demultiplexer_1_out27,
       demultiplexer_1_out28, demultiplexer_1_out29, demultiplexer_1_out30, demultiplexer_1_out31,
       demultiplexer_1_out32, demultiplexer_1_out33, demultiplexer_1_out34, demultiplexer_1_out35,
       demultiplexer_1_out36, demultiplexer_1_out37, demultiplexer_1_out38, demultiplexer_1_out39,
       demultiplexer_1_out40, demultiplexer_1_out41, demultiplexer_1_out42, demultiplexer_1_out43,
       demultiplexer_1_out44, demultiplexer_1_out45, demultiplexer_1_out46, demultiplexer_1_out47,
       demultiplexer_1_out48, demultiplexer_1_out49, demultiplexer_1_out50, demultiplexer_1_out51,
       demultiplexer_1_out52, demultiplexer_1_out53, demultiplexer_1_out54, demultiplexer_1_out55,
       demultiplexer_1_out56, demultiplexer_1_out57, demultiplexer_1_out58, demultiplexer_1_out59,
       demultiplexer_1_out60, demultiplexer_1_out61, demultiplexer_1_out62, demultiplexer_1_out63;
  wire [63:0] register_1_q, register_2_q, register_3_q, register_4_q, register_5_q, register_6_q,
       register_7_q, register_8_q, register_9_q, register_10_q, register_11_q, register_12_q, register_13_q,
       register_14_q, register_15_q, register_16_q, register_17_q, register_18_q, register_19_q,
       register_20_q, register_21_q, register_22_q, register_23_q, register_24_q, register_25_q,
       register_26_q, register_27_q, register_28_q, register_29_q, register_30_q, register_31_q,
       register_32_q, register_33_q, register_34_q, register_35_q, register_36_q, register_37_q,
       register_38_q, register_39_q, register_40_q, register_41_q, register_42_q, register_43_q,
       register_44_q, register_45_q, register_46_q, register_47_q, register_48_q, register_49_q,
       register_50_q, register_51_q, register_52_q, register_53_q, register_54_q, register_55_q,
       register_56_q, register_57_q, register_58_q, register_59_q, register_60_q, register_61_q,
       register_62_q, register_63_q, register_64_q;

  Demultiplexer #(.select(6)) demultiplexer_1 (
    .out0(demultiplexer_1_out0), .out1(demultiplexer_1_out1), .out2(demultiplexer_1_out2),
    .out3(demultiplexer_1_out3), .out4(demultiplexer_1_out4), .out5(demultiplexer_1_out5),
    .out6(demultiplexer_1_out6), .out7(demultiplexer_1_out7), .out8(demultiplexer_1_out8),
    .out9(demultiplexer_1_out9), .out10(demultiplexer_1_out10), .out11(demultiplexer_1_out11),
    .out12(demultiplexer_1_out12), .out13(demultiplexer_1_out13), .out14(demultiplexer_1_out14),
    .out15(demultiplexer_1_out15), .out16(demultiplexer_1_out16), .out17(demultiplexer_1_out17),
    .out18(demultiplexer_1_out18), .out19(demultiplexer_1_out19), .out20(demultiplexer_1_out20),
    .out21(demultiplexer_1_out21), .out22(demultiplexer_1_out22), .out23(demultiplexer_1_out23),
    .out24(demultiplexer_1_out24), .out25(demultiplexer_1_out25), .out26(demultiplexer_1_out26),
    .out27(demultiplexer_1_out27), .out28(demultiplexer_1_out28), .out29(demultiplexer_1_out29),
    .out30(demultiplexer_1_out30), .out31(demultiplexer_1_out31), .out32(demultiplexer_1_out32),
    .out33(demultiplexer_1_out33), .out34(demultiplexer_1_out34), .out35(demultiplexer_1_out35),
    .out36(demultiplexer_1_out36), .out37(demultiplexer_1_out37), .out38(demultiplexer_1_out38),
    .out39(demultiplexer_1_out39), .out40(demultiplexer_1_out40), .out41(demultiplexer_1_out41),
    .out42(demultiplexer_1_out42), .out43(demultiplexer_1_out43), .out44(demultiplexer_1_out44),
    .out45(demultiplexer_1_out45), .out46(demultiplexer_1_out46), .out47(demultiplexer_1_out47),
    .out48(demultiplexer_1_out48), .out49(demultiplexer_1_out49), .out50(demultiplexer_1_out50),
    .out51(demultiplexer_1_out51), .out52(demultiplexer_1_out52), .out53(demultiplexer_1_out53),
    .out54(demultiplexer_1_out54), .out55(demultiplexer_1_out55), .out56(demultiplexer_1_out56),
    .out57(demultiplexer_1_out57), .out58(demultiplexer_1_out58), .out59(demultiplexer_1_out59),
    .out60(demultiplexer_1_out60), .out61(demultiplexer_1_out61), .out62(demultiplexer_1_out62),
    .out63(demultiplexer_1_out63), .in(update), .sel(regX));
  Register #(.width(64)) register_1 (
    .D(value), .en(demultiplexer_1_out0), .clk(clock_1_out), .Q(register_1_q));  // open: clr
  Clock clock_1 (.out(clock_1_out));
  Register #(.width(64)) register_2 (
    .D(value), .en(demultiplexer_1_out8), .clk(clock_2_out), .Q(register_2_q));  // open: clr
  Clock clock_2 (.out(clock_2_out));
  Register #(.width(64)) register_3 (
    .D(value), .en(demultiplexer_1_out16), .clk(clock_3_out), .Q(register_3_q));  // open: clr
  Clock clock_3 (.out(clock_3_out));
  Register #(.width(64)) register_4 (
    .D(value), .en(demultiplexer_1_out24), .clk(clock_4_out), .Q(register_4_q));  // open: clr
  Clock clock_4 (.out(clock_4_out));
  Register #(.width(64)) register_5 (
    .D(value), .en(demultiplexer_1_out32), .clk(clock_5_out), .Q(register_5_q));  // open: clr
  Clock clock_5 (.out(clock_5_out));
  Register #(.width(64)) register_6 (
    .D(value), .en(demultiplexer_1_out40), .clk(clock_6_out), .Q(register_6_q));  // open: clr
  Clock clock_6 (.out(clock_6_out));
  Register #(.width(64)) register_7 (
    .D(value), .en(demultiplexer_1_out48), .clk(clock_7_out), .Q(register_7_q));  // open: clr
  Clock clock_7 (.out(clock_7_out));
  Register #(.width(64)) register_8 (
    .D(value), .en(demultiplexer_1_out56), .clk(clock_8_out), .Q(register_8_q));  // open: clr
  Clock clock_8 (.out(clock_8_out));
  Register #(.width(64)) register_9 (
    .D(value), .en(demultiplexer_1_out1), .clk(clock_9_out), .Q(register_9_q));  // open: clr
  Clock clock_9 (.out(clock_9_out));
  Register #(.width(64)) register_10 (
    .D(value), .en(demultiplexer_1_out9), .clk(clock_10_out), .Q(register_10_q));  // open: clr
  Clock clock_10 (.out(clock_10_out));
  Register #(.width(64)) register_11 (
    .D(value), .en(demultiplexer_1_out17), .clk(clock_11_out), .Q(register_11_q));  // open: clr
  Clock clock_11 (.out(clock_11_out));
  Register #(.width(64)) register_12 (
    .D(value), .en(demultiplexer_1_out25), .clk(clock_12_out), .Q(register_12_q));  // open: clr
  Clock clock_12 (.out(clock_12_out));
  Register #(.width(64)) register_13 (
    .D(value), .en(demultiplexer_1_out33), .clk(clock_13_out), .Q(register_13_q));  // open: clr
  Clock clock_13 (.out(clock_13_out));
  Register #(.width(64)) register_14 (
    .D(value), .en(demultiplexer_1_out41), .clk(clock_14_out), .Q(register_14_q));  // open: clr
  Clock clock_14 (.out(clock_14_out));
  Register #(.width(64)) register_15 (
    .D(value), .en(demultiplexer_1_out49), .clk(clock_15_out), .Q(register_15_q));  // open: clr
  Clock clock_15 (.out(clock_15_out));
  Register #(.width(64)) register_16 (
    .D(value), .en(demultiplexer_1_out57), .clk(clock_16_out), .Q(register_16_q));  // open: clr
  Clock clock_16 (.out(clock_16_out));
  Register #(.width(64)) register_17 (
    .D(value), .en(demultiplexer_1_out2), .clk(clock_17_out), .Q(register_17_q));  // open: clr
  Clock clock_17 (.out(clock_17_out));
  Register #(.width(64)) register_18 (
    .D(value), .en(demultiplexer_1_out10), .clk(clock_18_out), .Q(register_18_q));  // open: clr
  Clock clock_18 (.out(clock_18_out));
  Register #(.width(64)) register_19 (
    .D(value), .en(demultiplexer_1_out18), .clk(clock_19_out), .Q(register_19_q));  // open: clr
  Clock clock_19 (.out(clock_19_out));
  Register #(.width(64)) register_20 (
    .D(value), .en(demultiplexer_1_out26), .clk(clock_20_out), .Q(register_20_q));  // open: clr
  Clock clock_20 (.out(clock_20_out));
  Register #(.width(64)) register_21 (
    .D(value), .en(demultiplexer_1_out34), .clk(clock_21_out), .Q(register_21_q));  // open: clr
  Clock clock_21 (.out(clock_21_out));
  Register #(.width(64)) register_22 (
    .D(value), .en(demultiplexer_1_out42), .clk(clock_22_out), .Q(register_22_q));  // open: clr
  Clock clock_22 (.out(clock_22_out));
  Register #(.width(64)) register_23 (
    .D(value), .en(demultiplexer_1_out50), .clk(clock_23_out), .Q(register_23_q));  // open: clr
  Clock clock_23 (.out(clock_23_out));
  Register #(.width(64)) register_24 (
    .D(value), .en(demultiplexer_1_out58), .clk(clock_24_out), .Q(register_24_q));  // open: clr
  Clock clock_24 (.out(clock_24_out));
  Register #(.width(64)) register_25 (
    .D(value), .en(demultiplexer_1_out3), .clk(clock_25_out), .Q(register_25_q));  // open: clr
  Clock clock_25 (.out(clock_25_out));
  Register #(.width(64)) register_26 (
    .D(value), .en(demultiplexer_1_out11), .clk(clock_26_out), .Q(register_26_q));  // open: clr
  Clock clock_26 (.out(clock_26_out));
  Register #(.width(64)) register_27 (
    .D(value), .en(demultiplexer_1_out19), .clk(clock_27_out), .Q(register_27_q));  // open: clr
  Clock clock_27 (.out(clock_27_out));
  Register #(.width(64)) register_28 (
    .D(value), .en(demultiplexer_1_out27), .clk(clock_28_out), .Q(register_28_q));  // open: clr
  Clock clock_28 (.out(clock_28_out));
  Register #(.width(64)) register_29 (
    .D(value), .en(demultiplexer_1_out35), .clk(clock_29_out), .Q(register_29_q));  // open: clr
  Clock clock_29 (.out(clock_29_out));
  Register #(.width(64)) register_30 (
    .D(value), .en(demultiplexer_1_out43), .clk(clock_30_out), .Q(register_30_q));  // open: clr
  Clock clock_30 (.out(clock_30_out));
  Register #(.width(64)) register_31 (
    .D(value), .en(demultiplexer_1_out51), .clk(clock_31_out), .Q(register_31_q));  // open: clr
  Clock clock_31 (.out(clock_31_out));
  Register #(.width(64)) register_32 (
    .D(value), .en(demultiplexer_1_out59), .clk(clock_32_out), .Q(register_32_q));  // open: clr
  Clock clock_32 (.out(clock_32_out));
  Register #(.width(64)) register_33 (
    .D(value), .en(demultiplexer_1_out4), .clk(clock_33_out), .Q(register_33_q));  // open: clr
  Clock clock_33 (.out(clock_33_out));
  Register #(.width(64)) register_34 (
    .D(value), .en(demultiplexer_1_out12), .clk(clock_34_out), .Q(register_34_q));  // open: clr
  Clock clock_34 (.out(clock_34_out));
  Register #(.width(64)) register_35 (
    .D(value), .en(demultiplexer_1_out20), .clk(clock_35_out), .Q(register_35_q));  // open: clr
  Clock clock_35 (.out(clock_35_out));
  Register #(.width(64)) register_36 (
    .D(value), .en(demultiplexer_1_out28), .clk(clock_36_out), .Q(register_36_q));  // open: clr
  Clock clock_36 (.out(clock_36_out));
  Register #(.width(64)) register_37 (
    .D(value), .en(demultiplexer_1_out36), .clk(clock_37_out), .Q(register_37_q));  // open: clr
  Clock clock_37 (.out(clock_37_out));
  Register #(.width(64)) register_38 (
    .D(value), .en(demultiplexer_1_out44), .clk(clock_38_out), .Q(register_38_q));  // open: clr
  Clock clock_38 (.out(clock_38_out));
  Register #(.width(64)) register_39 (
    .D(value), .en(demultiplexer_1_out52), .clk(clock_39_out), .Q(register_39_q));  // open: clr
  Clock clock_39 (.out(clock_39_out));
  Register #(.width(64)) register_40 (
    .D(value), .en(demultiplexer_1_out60), .clk(clock_40_out), .Q(register_40_q));  // open: clr
  Clock clock_40 (.out(clock_40_out));
  Register #(.width(64)) register_41 (
    .D(value), .en(demultiplexer_1_out5), .clk(clock_41_out), .Q(register_41_q));  // open: clr
  Clock clock_41 (.out(clock_41_out));
  Register #(.width(64)) register_42 (
    .D(value), .en(demultiplexer_1_out13), .clk(clock_42_out), .Q(register_42_q));  // open: clr
  Clock clock_42 (.out(clock_42_out));
  Register #(.width(64)) register_43 (
    .D(value), .en(demultiplexer_1_out21), .clk(clock_43_out), .Q(register_43_q));  // open: clr
  Clock clock_43 (.out(clock_43_out));
  Register #(.width(64)) register_44 (
    .D(value), .en(demultiplexer_1_out29), .clk(clock_44_out), .Q(register_44_q));  // open: clr
  Clock clock_44 (.out(clock_44_out));
  Register #(.width(64)) register_45 (
    .D(value), .en(demultiplexer_1_out37), .clk(clock_45_out), .Q(register_45_q));  // open: clr
  Clock clock_45 (.out(clock_45_out));
  Register #(.width(64)) register_46 (
    .D(value), .en(demultiplexer_1_out45), .clk(clock_46_out), .Q(register_46_q));  // open: clr
  Clock clock_46 (.out(clock_46_out));
  Register #(.width(64)) register_47 (
    .D(value), .en(demultiplexer_1_out53), .clk(clock_47_out), .Q(register_47_q));  // open: clr
  Clock clock_47 (.out(clock_47_out));
  Register #(.width(64)) register_48 (
    .D(value), .en(demultiplexer_1_out61), .clk(clock_48_out), .Q(register_48_q));  // open: clr
  Clock clock_48 (.out(clock_48_out));
  Register #(.width(64)) register_49 (
    .D(value), .en(demultiplexer_1_out6), .clk(clock_49_out), .Q(register_49_q));  // open: clr
  Clock clock_49 (.out(clock_49_out));
  Register #(.width(64)) register_50 (
    .D(value), .en(demultiplexer_1_out14), .clk(clock_50_out), .Q(register_50_q));  // open: clr
  Clock clock_50 (.out(clock_50_out));
  Register #(.width(64)) register_51 (
    .D(value), .en(demultiplexer_1_out22), .clk(clock_51_out), .Q(register_51_q));  // open: clr
  Clock clock_51 (.out(clock_51_out));
  Register #(.width(64)) register_52 (
    .D(value), .en(demultiplexer_1_out30), .clk(clock_52_out), .Q(register_52_q));  // open: clr
  Clock clock_52 (.out(clock_52_out));
  Register #(.width(64)) register_53 (
    .D(value), .en(demultiplexer_1_out38), .clk(clock_53_out), .Q(register_53_q));  // open: clr
  Clock clock_53 (.out(clock_53_out));
  Register #(.width(64)) register_54 (
    .D(value), .en(demultiplexer_1_out46), .clk(clock_54_out), .Q(register_54_q));  // open: clr
  Clock clock_54 (.out(clock_54_out));
  Register #(.width(64)) register_55 (
    .D(value), .en(demultiplexer_1_out54), .clk(clock_55_out), .Q(register_55_q));  // open: clr
  Clock clock_55 (.out(clock_55_out));
  Register #(.width(64)) register_56 (
    .D(value), .en(demultiplexer_1_out62), .clk(clock_56_out), .Q(register_56_q));  // open: clr
  Clock clock_56 (.out(clock_56_out));
  Register #(.width(64)) register_57 (
    .D(value), .en(demultiplexer_1_out7), .clk(clock_57_out), .Q(register_57_q));  // open: clr
  Clock clock_57 (.out(clock_57_out));
  Register #(.width(64)) register_58 (
    .D(value), .en(demultiplexer_1_out15), .clk(clock_58_out), .Q(register_58_q));  // open: clr
  Clock clock_58 (.out(clock_58_out));
  Register #(.width(64)) register_59 (
    .D(value), .en(demultiplexer_1_out23), .clk(clock_59_out), .Q(register_59_q));  // open: clr
  Clock clock_59 (.out(clock_59_out));
  Register #(.width(64)) register_60 (
    .D(value), .en(demultiplexer_1_out31), .clk(clock_60_out), .Q(register_60_q));  // open: clr
  Clock clock_60 (.out(clock_60_out));
  Register #(.width(64)) register_61 (
    .D(value), .en(demultiplexer_1_out39), .clk(clock_61_out), .Q(register_61_q));  // open: clr
  Clock clock_61 (.out(clock_61_out));
  Register #(.width(64)) register_62 (
    .D(value), .en(demultiplexer_1_out47), .clk(clock_62_out), .Q(register_62_q));  // open: clr
  Clock clock_62 (.out(clock_62_out));
  Register #(.width(64)) register_63 (
    .D(value), .en(demultiplexer_1_out55), .clk(clock_63_out), .Q(register_63_q));  // open: clr
  Clock clock_63 (.out(clock_63_out));
  Register #(.width(64)) register_64 (
    .D(value), .en(demultiplexer_1_out63), .clk(clock_64_out), .Q(register_64_q));  // open: clr
  Clock clock_64 (.out(clock_64_out));
  Multiplexer #(.select(6), .width(64)) multiplexer_1 (
    .in0(register_1_q), .in1(register_9_q), .in2(register_17_q), .in3(register_25_q), .in4(register_33_q),
    .in5(register_41_q), .in6(register_49_q), .in7(register_57_q), .in8(register_2_q), .in9(register_10_q),
    .in10(register_18_q), .in11(register_26_q), .in12(register_34_q), .in13(register_42_q),
    .in14(register_50_q), .in15(register_58_q), .in16(register_3_q), .in17(register_11_q),
    .in18(register_19_q), .in19(register_27_q), .in20(register_35_q), .in21(register_43_q),
    .in22(register_51_q), .in23(register_59_q), .in24(register_4_q), .in25(register_12_q),
    .in26(register_20_q), .in27(register_28_q), .in28(register_36_q), .in29(register_44_q),
    .in30(register_52_q), .in31(register_60_q), .in32(register_5_q), .in33(register_13_q),
    .in34(register_21_q), .in35(register_29_q), .in36(register_37_q), .in37(register_45_q),
    .in38(register_53_q), .in39(register_61_q), .in40(register_6_q), .in41(register_14_q),
    .in42(register_22_q), .in43(register_30_q), .in44(register_38_q), .in45(register_46_q),
    .in46(register_54_q), .in47(register_62_q), .in48(register_7_q), .in49(register_15_q),
    .in50(register_23_q), .in51(register_31_q), .in52(register_39_q), .in53(register_47_q),
    .in54(register_55_q), .in55(register_63_q), .in56(register_8_q), .in57(register_16_q),
    .in58(register_24_q), .in59(register_32_q), .in60(register_40_q), .in61(register_48_q),
    .in62(register_56_q), .in63(register_64_q), .out(regXout), .sel(regX));
  Multiplexer #(.select(6), .width(64)) multiplexer_2 (
    .in0(register_1_q), .in1(register_9_q), .in2(register_17_q), .in3(register_25_q), .in4(register_33_q),
    .in5(register_41_q), .in6(register_49_q), .in7(register_57_q), .in8(register_2_q), .in9(register_10_q),
    .in10(register_18_q), .in11(register_26_q), .in12(register_34_q), .in13(register_42_q),
    .in14(register_50_q), .in15(register_58_q), .in16(register_3_q), .in17(register_11_q),
    .in18(register_19_q), .in19(register_27_q), .in20(register_35_q), .in21(register_43_q),
    .in22(register_51_q), .in23(register_59_q), .in24(register_4_q), .in25(register_12_q),
    .in26(register_20_q), .in27(register_28_q), .in28(register_36_q), .in29(register_44_q),
    .in30(register_52_q), .in31(register_60_q), .in32(register_5_q), .in33(register_13_q),
    .in34(register_21_q), .in35(register_29_q), .in36(register_37_q), .in37(register_45_q),
    .in38(register_53_q), .in39(register_61_q), .in40(register_6_q), .in41(register_14_q),
    .in42(register_22_q), .in43(register_30_q), .in44(register_38_q), .in45(register_46_q),
    .in46(register_54_q), .in47(register_62_q), .in48(register_7_q), .in49(register_15_q),
    .in50(register_23_q), .in51(register_31_q), .in52(register_39_q), .in53(register_47_q),
    .in54(register_55_q), .in55(register_63_q), .in56(register_8_q), .in57(register_16_q),
    .in58(register_24_q), .in59(register_32_q), .in60(register_40_q), .in61(register_48_q),
    .in62(register_56_q), .in63(register_64_q), .out(regYout), .sel(regY));
endmodule
